# Fritzing sketch led_flash (saved by Fritzing 0.9.2b)
breadboards: 1

parts:
  元件1 = Arduino Uno (Rev3)
  LED1 = LED - 5mm [color="Red (633nm)" package="5 mm [THT]"]
  LED2 = LED - 5mm [color="Blue (525nm)" package="5 mm [THT]"]
  LED3 = LED - 5mm [color="Green (570nm)" package="5 mm [THT]"]

nets:
  N1: 元件1.D8, LED3.cathode
  N2: 元件1.D12/MISO, LED2.cathode
  N3: 元件1.D13/SCK, LED1.cathode
  N4: 元件1.GND, LED1.anode, LED2.anode, LED3.anode

// code stored in the sketch: led_flash.ino
const int BLUE_LED = 12;
const int GREEN_LED = 8;
const int RED_LED = 13;
const int FAN = 10;
//1.63, 85
//3.86 , 200
//4 , 210
//4.95, 255
const int FAN_LEVEL = 210;

void setup() {
  // put your setup code here, to run once:
  pinMode(BLUE_LED, OUTPUT);
  pinMode(GREEN_LED, OUTPUT);
  pinMode(RED_LED, OUTPUT);
  pinMode(FAN, OUTPUT);
}

void loop() {
  // put your main code here, to run repeatedly:
  digitalWrite(BLUE_LED, HIGH);
  delay(1000);
  digitalWrite(BLUE_LED, LOW);
  delay(1000);
  digitalWrite(RED_LED, HIGH);
  delay(1000);
  digitalWrite(RED_LED, LOW);
  delay(1000);
  digitalWrite(GREEN_LED, HIGH);
  delay(1000);
  digitalWrite(GREEN_LED, LOW);
  delay(1000);
  analogWrite(FAN, FAN_LEVEL);
  delay(10000);
}
