# Fritzing sketch led_flash (saved by Fritzing 0.9.2b)
breadboards: 1

parts:
  元件1 = Arduino Uno (Rev3)
  LED1 = LED - 5mm [color="Red (633nm)" package="5 mm [THT]"]
  LED2 = LED - 5mm [color="Blue (525nm)" package="5 mm [THT]"]
  LED3 = LED - 5mm [color="Green (570nm)" package="5 mm [THT]"]

nets:
  N1: 元件1.D8, LED3.cathode
  N2: 元件1.D12/MISO, LED2.cathode
  N3: 元件1.D13/SCK, LED1.cathode
  N4: 元件1.GND, LED1.anode, LED2.anode, LED3.anode
