# Fritzing sketch layout (saved by Fritzing 0.9.2b)
breadboards: 1

parts:
  元件1 = Arduino Uno (Rev3)
  LED1 = LED - 5mm [color="Red (633nm)" package="5 mm [THT]"]
  LED2 = LED - 5mm [color="Blue (470nm)" package="5 mm [THT]"]
  LED3 = LED - 5mm [color="Green (570nm)" package="5 mm [THT]"]
  U1 = RELAY [package=relay-g5q]
  VCC1 = 4 x AAA Battery Mount
  M1 = DC Motor

nets:
  N1: 元件1.D8, 元件1.D12/MISO, 元件1.D13/SCK, 元件1.GND, LED1.cathode, LED1.anode, LED2.cathode, LED2.anode, LED3.cathode, LED3.anode
  N2: 元件1.D4, 元件1.D7, U1.MAIN
  N3: U1.COIL2, M1.pin_1
  N4: U1.NO, VCC1.+
